// Logisim project Lab4.circ as structural Verilog: 3 circuits, main circuit main
module main (
  input  A,
  input  B,
  input  L,
  output S,
  output P
);

  wire and_1_out, and_2_out, and_3_out, and_4_out, and_5_out, and_6_out, and_7_out, not_1_out, not_2_out,
       not_3_out;

  not not_1 (not_1_out, A);
  not not_2 (not_2_out, B);
  not not_3 (not_3_out, L);
  and and_1 (and_1_out, not_1_out, not_2_out, L);
  or or_1 (S, and_1_out, and_2_out, and_3_out, and_4_out);
  and and_2 (and_2_out, not_1_out, B, not_3_out);
  and and_3 (and_3_out, A, not_2_out, not_3_out);
  and and_4 (and_4_out, A, B, L);
  and and_5 (and_5_out, A, B);
  or or_2 (P, and_5_out, and_6_out, and_7_out);
  and and_6 (and_6_out, A, L);
  and and_7 (and_7_out, B, L);
endmodule

module EightBitSum (
  input  [7:0] in_1,
  input  [7:0] in_2,
  output [7:0] out_3
);

  wire main_1_p, main_2_p, main_3_p, main_4_p, main_5_p, main_6_p, main_7_p;

  main main_1 (.A(in_1[0]), .B(in_2[0]), .S(out_3[0]), .P(main_1_p));  // open: L
  main main_2 (.A(in_1[1]), .B(in_2[1]), .L(main_1_p), .S(out_3[1]), .P(main_2_p));
  main main_3 (.A(in_1[2]), .B(in_2[2]), .L(main_2_p), .S(out_3[2]), .P(main_3_p));
  main main_4 (.A(in_1[3]), .B(in_2[3]), .L(main_3_p), .S(out_3[3]), .P(main_4_p));
  main main_5 (.A(in_1[4]), .B(in_2[4]), .L(main_4_p), .S(out_3[4]), .P(main_5_p));
  main main_6 (.A(in_1[5]), .B(in_2[5]), .L(main_5_p), .S(out_3[5]), .P(main_6_p));
  main main_7 (.A(in_1[6]), .B(in_2[6]), .L(main_6_p), .S(out_3[6]), .P(main_7_p));
  main main_8 (.A(in_1[7]), .B(in_2[7]), .L(main_7_p), .S(out_3[7]));  // open: P
endmodule

module Step (
  input  A,
  input  B,
  input  C,
  input  D,
  output [3:0] out_5
);

  wire and_1_out, and_2_out, and_3_out, and_4_out, and_5_out, and_6_out, and_7_out, not_1_out, not_2_out,
       not_3_out, or_3_out;

  and and_1 (and_1_out, A, C);
  not not_1 (not_1_out, A);
  not not_2 (not_2_out, B);
  not not_3 (not_3_out, C);
  and and_2 (and_2_out, B, not_3_out);
  or or_1 (out_5[3], and_1_out, and_2_out);
  and and_3 (and_3_out, A, B);
  or or_2 (out_5[2], and_3_out, and_4_out);
  and and_4 (and_4_out, not_1_out, not_2_out);
  and and_5 (and_5_out, A, not_2_out);
  and and_6 (and_6_out, A, C);
  or or_3 (or_3_out, and_5_out, and_6_out);
  or or_4 (out_5[1], or_3_out, and_7_out);
  and and_7 (and_7_out, not_2_out, C);

  assign out_5[0] = D;
endmodule
