// Logisim project lab5.circ as structural Verilog: 1 circuit, main circuit main
module main (
  input  in_1,
  output [3:0] out_2
);

  wire and_1_out, and_2_out, and_3_out, clock_1_out, t_ff_1_qn, t_ff_2_qn, t_ff_3_qn;

  Clock clock_1 (.out(clock_1_out));
  and and_1 (and_1_out, in_1, t_ff_1_qn);
  T_Flip_Flop t_ff_1 (.T(in_1), .clk(clock_1_out), .Q(out_2[0]), .Qn(t_ff_1_qn));  // open: reset, preset
  T_Flip_Flop t_ff_2 (.T(and_1_out), .clk(clock_1_out), .Q(out_2[1]), .Qn(t_ff_2_qn));  // open: reset, preset
  T_Flip_Flop t_ff_3 (.T(and_2_out), .clk(clock_1_out), .Q(out_2[2]), .Qn(t_ff_3_qn));  // open: reset, preset
  T_Flip_Flop t_ff_4 (.T(and_3_out), .clk(clock_1_out), .Q(out_2[3]));  // open: Qn, reset, preset
  and and_2 (and_2_out, t_ff_2_qn, t_ff_1_qn, in_1);
  and and_3 (and_3_out, t_ff_3_qn, t_ff_2_qn, t_ff_1_qn, in_1);
endmodule
